# Fritzing sketch schemat_1 (saved by Fritzing 0.9.3b)
breadboards: 1

parts:
  Mod1 = Raspberry Pi 4B
  J1 = Piezo Speaker
  R1 = Resistor [tolerance=±5% resistance=220 package=THT]

nets:
  N1: Mod1.GND, R1.Pin_1
  N2: Mod1.GPIO4, J1.pin2
  N3: J1.pin1, R1.Pin_0
