# Fritzing sketch schemat_2 (saved by Fritzing 0.9.3b)
breadboards: 1

parts:
  Mod1 = Raspberry Pi 4B
  hc-sr1 = hc-sr04
  Part1 = Logic Level Converter

nets:
  N1: Mod1.3V3, Part1.LV
  5V: Mod1.5V, hc-sr1.VCC, Part1.HV
  GND: Mod1.GND, hc-sr1.GND, Part1.GND
  N2: Mod1.GPIO27, Part1.RX_LV
  N3: Mod1.GPIO19, Part1.TX_LV
  N4: hc-sr1.Trig, Part1.TX_HV
  N5: hc-sr1.Echo, Part1.RX_HV
