# Fritzing sketch schemat (saved by Fritzing 0.9.3b)
breadboards: 1

parts:
  Mod1 = Raspberry Pi 4B
  LCD1 = LCD screen
  LCM1602_IIC1 = LCM1602 IIC [part_number="LCM1602 IIC" chip_label="LCM1602 IIC" package="DIP (Dual Inline) [THT]"]
  Part1 = Logic Level Converter
  J1 = Piezo Speaker
  R2 = Resistor [tolerance=±5% resistance=220 package="2010 [SMD]"]
  R3 = Resistor [tolerance=±5% resistance=220 package="2010 [SMD]"]
  DHT11_1 = DHT11 module
  R4 = Resistor [tolerance=±5% resistance=220 package=THT]
  R5 = Resistor [tolerance=±5% resistance=220 package=THT]

nets:
  N1: Mod1.3V3, Part1.LV
  5V: Mod1.5V, Mod1.GPIO2, LCM1602_IIC1.VCC, Part1.HV, R3.Pin_0, R4.Pin_1
  GND: Mod1.GPIO3, Mod1.GND, Mod1.GPIO7, LCM1602_IIC1.GND, Part1.GND, J1.pin1, DHT11_1.GND, R5.Pin_1
  N2: Mod1.GPIO4, Mod1.GPIO14, Part1.TX2_LV
  VSS: LCD1.VSS, LCM1602_IIC1.VSS
  VDD: LCD1.VDD, LCM1602_IIC1.VDD
  N3: LCD1.V0, LCM1602_IIC1.V0
  N4: LCD1.RS, LCM1602_IIC1.RS
  N5: LCD1.R/W, LCM1602_IIC1.RW
  N6: LCD1.E, LCM1602_IIC1.E
  N7: LCD1.DB0, LCM1602_IIC1.D0
  N8: LCD1.DB1, LCM1602_IIC1.D1
  N9: LCD1.DB2, LCM1602_IIC1.D2
  N10: LCD1.DB3, LCM1602_IIC1.D3
  N11: LCD1.DB4, LCM1602_IIC1.D4
  N12: LCD1.DB5, LCM1602_IIC1.D5
  N13: LCD1.DB6, LCM1602_IIC1.D6
  N14: LCD1.DB7, LCM1602_IIC1.D7
  N15: LCD1.LED+, LCM1602_IIC1.A
  N16: LCD1.LED-, LCM1602_IIC1.K
  N17: LCM1602_IIC1.SDA, Part1.RX_HV
  N18: LCM1602_IIC1.SCL, Part1.TX_HV
  N19: Part1.RX_LV, R4.Pin_0
  N20: Part1.TX_LV, R5.Pin_0
  N21: Part1.RX2_HV, R2.Pin_0
  N22: Part1.TX2_HV, DHT11_1.DATA
  N23: J1.pin2, R2.Pin_1
  N24: R3.Pin_1, DHT11_1.VCC

custom parts:
  LCM1602 IIC: I2C-Module to use a 1602 or 2004 LCD on with the wire.h libory Serial LCD Modul
  DHT11 module: https://cdn-learn.adafruit.com/downloads/pdf/dht.pdf DHT11 black pcb module reference by:https://github.com/adafruit/Fritzing-Library/blob/master/parts/DHT11%20Humitidy%20and%20Temperature%20Sensor.fzpz
