# Fritzing sketch schemat_nowy (saved by Fritzing 0.9.3b)
breadboards: 1

parts:
  Mod1 = Raspberry Pi 4B
  hc-sr1 = hc-sr04
  Part1 = Logic Level Converter
  J1 = Piezo Speaker
  R1 = Resistor [tolerance=±5% resistance=220 package=THT]

nets:
  N1: Mod1.3V3, Part1.LV
  5V: Mod1.5V, hc-sr1.VCC, Part1.HV
  GND: Mod1.GND, hc-sr1.GND, Part1.GND, J1.pin1
  N2: Mod1.GPIO17, R1.Pin_1
  N3: Mod1.GPIO27, Part1.RX_LV
  N4: Mod1.GPIO19, Part1.TX_LV
  N5: hc-sr1.Trig, Part1.TX_HV
  N6: hc-sr1.Echo, Part1.RX_HV
  N7: J1.pin2, R1.Pin_0
